# Fritzing sketch 고정밀 ph 측정기-bread (saved by Fritzing 0.9.3b)

parts:
  Adafruit_ADS1115 = Adafruit ADS1115 16Bit I2C ADC [part_number="Adafruit #1085"]
  아두이노_나노 = Arduino Nano (Rev3.0)
  DS18B20_온도센서 = DS18B20 1-Wire Temperature Sensor Probe Cable
  Star_Grount_Point = STARBOARD_GND [package=starboard_ground_small2]
  HC-06 = Bluetooth HC-06u [package=THT]
  R2 = Resistor [tolerance=±5% resistance=4.7k package=THT]
  L298N1-_5VEN_off = L298N DC motor driver
  L298N2-_5VEN_off = L298N DC motor driver
  L298N3-_5VEN_off_ENA_on_ENB_on = L298N DC motor driver
  R5 = Resistor [tolerance=±20% resistance=20k package=THT]
  R4 = Resistor [tolerance=±5% resistance=10k package=THT]
  12V_DC_잭 = 2.1mm Barrel Jack with Terminal Block
  5V_USB_펌프_-_참조물_에어_공급 = 6V Mini Solenoid Valve 3-Way (SZH-GNP114)
  연동_펌프1 = Peristaltic Dosing Pump 12V (NKP-DC-B06B)
  연동_펌프2 = Peristaltic Dosing Pump 12V (NKP-DC-B06B)
  연동_펌프3 = Peristaltic Dosing Pump 12V (NKP-DC-B06B)
  연동_펌프4 = Peristaltic Dosing Pump 12V (NKP-DC-B06B)
  5V_USB_펌프_-_수조물_에어_공급 = 6V Mini Solenoid Valve 3-Way (SZH-GNP114)
  12V_->_5V = 5V Fixed DC-DC Buck Converter 3A (SZH-PWSD-016)
  DC_모터_PWM_속도_조절(1~4) = PWM DC Motor Speed Controller 2A (SZH-MSC-009)
  U2 = PWM DC Motor Speed Controller 2A (SZH-MSC-009)
  U3 = PWM DC Motor Speed Controller 2A (SZH-MSC-009)
  U4 = PWM DC Motor Speed Controller 2A (SZH-MSC-009)
  C1[X] = Ceramic Capacitor [capacitance="100 nF" package="1206 [SMD, multilayer]"]
  C2[X] = Ceramic Capacitor [capacitance="100 nF" package="1206 [SMD, multilayer]"]
  C3[X] = Ceramic Capacitor [capacitance="100 nF" package="1206 [SMD, multilayer]"]
  R6[X] = Resistor [tolerance=±20% resistance=330 package=THT]
  C4[X] = Ceramic Capacitor [capacitance="100 nF" package="1206 [SMD, multilayer]"]
  PROBE1 = Gravity pH Probe Laboratory Grade (SEN0161-V2)
  DFRobot_SEN0161_pH_미터_V2 = Gravity pH Meter V2 Signal Board (SEN0161-V2)

nets:
  N1: Adafruit_ADS1115.AIN0, R6[X].Pin_1, C4[X].1
  N2: Adafruit_ADS1115.SDA, 아두이노_나노.A4
  N3: Adafruit_ADS1115.SCL, 아두이노_나노.A5
  GND: Adafruit_ADS1115.GND, 아두이노_나노.GND, DS18B20_온도센서.GND, DS18B20_온도센서.DQ, Star_Grount_Point.MOUNT, HC-06.GND, L298N1-_5VEN_off.GND, L298N2-_5VEN_off.GND, L298N3-_5VEN_off_ENA_on_ENB_on.GND, R5.Pin_0, 12V_DC_잭.NEG, 12V_->_5V.IN-, 12V_->_5V.OUT-, C1[X].0, C2[X].1, C3[X].1, C4[X].0, DFRobot_SEN0161_pH_미터_V2.GND
  5V: Adafruit_ADS1115.VDD, 아두이노_나노.5V, DS18B20_온도센서.VDD, HC-06.VCC, R2.Pin_1, L298N1-_5VEN_off.5V, L298N2-_5VEN_off.5V, L298N3-_5VEN_off_ENA_on_ENB_on.12V, L298N3-_5VEN_off_ENA_on_ENB_on.5V#7, 12V_->_5V.OUT+, C1[X].1, C2[X].0, C3[X].0, DFRobot_SEN0161_pH_미터_V2.V+
  N4: 아두이노_나노.D1/TX, R4.Pin_0
  N5: 아두이노_나노.D0/RX, HC-06.TXD
  N6: 아두이노_나노.D4, L298N1-_5VEN_off.IN4
  N7: 아두이노_나노.D5, L298N1-_5VEN_off.IN3
  N8: 아두이노_나노.D6, L298N1-_5VEN_off.IN2
  N9: 아두이노_나노.D7, L298N1-_5VEN_off.IN1
  N10: 아두이노_나노.D8, L298N2-_5VEN_off.IN4
  N11: 아두이노_나노.D9, L298N2-_5VEN_off.IN3
  N12: 아두이노_나노.D10, L298N2-_5VEN_off.IN2
  N13: 아두이노_나노.D11/MOSI, L298N2-_5VEN_off.IN1
  N14: 아두이노_나노.D12/MISO, L298N3-_5VEN_off_ENA_on_ENB_on.IN3
  N15: 아두이노_나노.A0, DS18B20_온도센서.shield, R2.Pin_0
  N16: 아두이노_나노.D13/SCK, L298N3-_5VEN_off_ENA_on_ENB_on.IN1
  N17: HC-06.RXD, R5.Pin_1, R4.Pin_1
  N18: L298N1-_5VEN_off.OUT1, 연동_펌프1.VCC+
  N19: L298N1-_5VEN_off.OUT2, 연동_펌프1.GND-
  N20: L298N1-_5VEN_off.OUT3, 연동_펌프2.VCC+
  N21: L298N1-_5VEN_off.OUT4, 연동_펌프2.GND-
  12V: L298N1-_5VEN_off.12V, L298N2-_5VEN_off.12V, 12V_DC_잭.POS, 12V_->_5V.IN+
  N22: L298N1-_5VEN_off.ENA, DC_모터_PWM_속도_조절(1~4).Motor-
  N23: L298N1-_5VEN_off.ENB, U2.Motor-
  N24: L298N2-_5VEN_off.OUT1, 연동_펌프3.VCC+
  N25: L298N2-_5VEN_off.OUT2, 연동_펌프3.GND-
  N26: L298N2-_5VEN_off.OUT3, 연동_펌프4.VCC+
  N27: L298N2-_5VEN_off.OUT4, 연동_펌프4.GND-
  N28: L298N2-_5VEN_off.ENA, U3.Motor-
  N29: L298N2-_5VEN_off.ENB, U4.Motor-
  N30: L298N3-_5VEN_off_ENA_on_ENB_on.OUT1, DC_모터_PWM_속도_조절(1~4).Power+, U2.Power+, U3.Power+, U4.Power+
  N31: L298N3-_5VEN_off_ENA_on_ENB_on.OUT2, DC_모터_PWM_속도_조절(1~4).Power-, U2.Power-, U3.Power-, U4.Power-
  VCC: L298N3-_5VEN_off_ENA_on_ENB_on.OUT3, 5V_USB_펌프_-_참조물_에어_공급.VCC, 5V_USB_펌프_-_수조물_에어_공급.VCC
  GND_2: L298N3-_5VEN_off_ENA_on_ENB_on.OUT4, 5V_USB_펌프_-_참조물_에어_공급.GND, 5V_USB_펌프_-_수조물_에어_공급.GND
  N32: L298N3-_5VEN_off_ENA_on_ENB_on.5V#9, L298N3-_5VEN_off_ENA_on_ENB_on.ENA
  N33: L298N3-_5VEN_off_ENA_on_ENB_on.5V#10, L298N3-_5VEN_off_ENA_on_ENB_on.ENB
  N34: R6[X].Pin_0, DFRobot_SEN0161_pH_미터_V2.A
  N35: PROBE1.BNC-, DFRobot_SEN0161_pH_미터_V2.BNC

notes:
  Star Ground Point
  (AGND-회색 & DGND-검은색 결합점)
  DGND - 회색, AGND - 검정
  결합점,
  전원 GND
  C1-C4 노이즈 콘데서
  필요없어서 제거,
  R6 330옴 RC 필터저항
  필요없어서 제거.
  [X] 제거 표시입니다.
  USB 펌프로
  교체했어요.
  ton 명령으로 작동
  airoff으로 끌수 있음.
  모터 속도 제어 전원
  ron 명령으로 속도조절 켜짐.
  ron 끄면, 최대 회전
  airoff 으로 끌 수 있음.
  (주의: 0V 최대, 5V 멈춤. motor - PWM 역신호 이용합니다.)

custom parts:
  Adafruit ADS1115 16Bit I2C ADC: For microcontrollers without an analog-to-digital converter or when you want a higher-precision ADC, the ADS1115 provides 16-bit precision at 860 samples/second over I2C. The chip can be configured as 4 single-ended input channels, or two differential channels. As a nice bonus, it even includes a programmable gain amplifier, up to x16, to help boost up smaller single/differential signals to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
  Bluetooth HC-06u: Bluetooth HC-06 - face up, pins down 16.5mm x 37.5mm PCB
  L298N DC motor driver: 2x DC motor driver with 78M05 positive voltage regulator (7..35 V) L298N: max 46 V, 2 A Set 5 V Enable jumper to enable 5 V regultor (needed for the L298N) and +5 V output at screw terminal or supply external +5 V at screw terminal Set ENA and/or ENB to +5 V to enable motor permanently or supply ENA and/or ENB with PWM signal IN1 and IN2 set rotation directory for motor A (OUT1/OUT2) IN2 and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
  6V Mini Solenoid Valve 3-Way (SZH-GNP114): 6V Mini 3-Way Solenoid Valve SZH-GNP114 (ZHY-0519). OFF: air flows IN-top to Port-A-left. ON: air flows IN-top to Port-B-right. 2-pin JST connector.
  Peristaltic Dosing Pump 12V (NKP-DC-B06B): Kamoer NKP-DC-B06B Peristaltic Dosing Pump. 12V DC / 0.15A. Flow 5.2~90ml/min. BPT silicone tube 2x4mm. 3-wheel. For Arduino aquarium/lab DIY. Size: 67x41x55mm.
  5V Fixed DC-DC Buck Converter 3A (SZH-PWSD-016): 5V Fixed Output Step-Down DC-DC Converter 3A. Input 7V-26V, Output 5V/3A, max 96% efficiency. SZH-PWSD-016.
  PWM DC Motor Speed Controller 2A (SZH-MSC-009): PWM DC Motor Speed Controller 2A SZH-MSC-009. Input DC 1.8V-15V, Max 30W/2A. Duty cycle 0-100% via potentiometer knob.
  Gravity pH Probe Laboratory Grade (SEN0161-V2): DFRobot Gravity Analog pH Probe Laboratory Grade. SEN0161-V2. Range 0-14 pH, 5-60°C, BNC connector, 100cm cable. Connect to Signal Board BNC port.
  Gravity pH Meter V2 Signal Board (SEN0161-V2): DFRobot Gravity Analog pH Sensor Signal Conversion Board V2. SEN0161-V2. Supply 3.3-5.5V, Output 0-3V, BNC probe connector, Gravity PH2.0-3P signal connector.
